# Fritzing sketch quantus (saved by Fritzing 0.9.2b)
circuit board: 8.46667cm x 5.64444cm
breadboards: 1

parts:
  Part1 = SRF05 Ultrasonic Rangefinder
  U1 = TMP36 [package=to-92-kit]
  R2 = Resistor [tolerance=±5% resistance=220 package="0805 [SMD]"]
  R5 = Resistor [tolerance=±5% resistance=220 package="0805 [SMD]"]
  Part2 = Intel Edison Arduinobreakout
  S2 = SPST Switch [package=switch-spdt_lock.007s]
  S3 = SPST Switch [package=switch-spdt_lock.007s]
  S4 = SPST Switch [package=switch-spdt_lock.007s]
  LED5 = smd LED [color="Green (555nm)" package="0805 [SMD]"]
  LED6 = smd LED [color="Green (555nm)" package="0805 [SMD]"]
  LED7 = smd LED [color="Green (555nm)" package="0805 [SMD]"]
  LED8 = RGB LED (com. anode, rbg) [package="5 mm [THT]"]
  U2 = SD_CARD_SOCKET [package=sdcard_4uconn]
  S1 = Pushbutton [package="[THT]"]
  VCC1 = Battery block 9V
  R7 = Resistor [tolerance=±5% resistance=220 package="0805 [SMD]"]
  R8 = Resistor [tolerance=±5% resistance=220 package="0805 [SMD]"]
  R9 = Resistor [tolerance=±5% resistance=220 package="0805 [SMD]"]

nets (from the breadboard view):
  VCC: Part1.VCC, U1.VCC, R5.Pin_1, Part2.5V, R7.Pin_1, R8.Pin_1, R9.Pin_1
  N1: Part1.Trig, Part2.D5_PWM
  N2: Part1.Echo, Part2.D6_PWM
  GND: Part1.GND, U1.GND, R2.Pin_1, Part2.GND, S2.S, S3.S, S4.S, LED5.cathode, LED6.cathode, LED7.cathode, U2.DAT0, VCC1.-
  N3: U1.VOUT, Part2.A0
  N4: R2.Pin_0, LED8.common_anode
  N5: R5.Pin_0, S1.Pin_3, S1.Pin_4
  N6: Part2.D8, S3.P, LED6.anode
  N7: Part2.D9_PWM, S4.P, LED7.anode
  N8: Part2.D10_PWM/SS, U2.WP
  N9: Part2.D11_PWM/MOSI, U2.DAT2
  N10: Part2.D12/MISO, U2.DAT1
  N11: Part2.D13/SCK, U2.CD
  N12: Part2.D0/RX, S1.Pin_1, S1.Pin_2
  N13: Part2.D1/TX, LED8.red_cathode
  N14: Part2.D3_PWM, LED8.green_cathode
  N15: Part2.D7, S2.P, LED5.anode
  N16: Part2.3V3, U2.VSS2
  N17: Part2.VIN, VCC1.+
  N18: S2.O, R7.Pin_0
  N19: S3.O, R8.Pin_0
  N20: S4.O, R9.Pin_0
